# Fritzing sketch full_bridge (saved by Fritzing 0.9.4)
breadboards: 1

parts:
  part = LOAD_CELL [package=1x03]
  part_2 = LOAD_CELL [package=1x03]
  part_3 = LOAD_CELL [package=1x03]
  part_4 = LOAD_CELL [package=1x03]
  part_5 = HX711 Weighing Sensor Module

nets:
  N1: part.B, part_2.B
  N2: part.W, part_5.E-
  N3: part.R, part_3.R
  N4: part_2.W, part_5.A+
  N5: part_2.R, part_4.R
  N6: part_3.B, part_4.B
  N7: part_3.W, part_5.A-
  N8: part_4.W, part_5.E+
